// Logisim project new.circ as structural Verilog: 1 circuit, main circuit main
module main (
  input  [7:0] in_1
);

  wire adder_1_cout, and_1_out, and_2_out, and_3_out, and_4_out, and_5_out, and_7_out, and_8_out, and_9_out,
       and_10_out, clock_1_out, comparator_1_eq, comparator_2_eq, comparator_3_eq, comparator_4_eq,
       comparator_5_eq, comparator_6_eq, comparator_7_eq, comparator_8_eq, comparator_9_eq, comparator_10_eq,
       comparator_11_eq, comparator_12_eq, comparator_12_lt, comparator_13_eq, comparator_14_eq,
       comparator_15_eq, comparator_16_eq, comparator_16_gt, comparator_17_eq, comparator_18_eq,
       comparator_19_lt, comparator_20_eq, comparator_21_eq, comparator_22_gt, comparator_23_eq,
       comparator_24_eq, comparator_25_eq, decoder_1_out0, decoder_1_out1, decoder_1_out2, decoder_1_out3,
       decoder_1_out5, decoder_2_out0, decoder_2_out1, decoder_2_out2, not_1_out, or_1_out, or_2_out,
       or_3_out, or_4_out, or_6_out, or_7_out, pc_carry, pull_resistor_1_node, pull_resistor_2_node,
       pull_resistor_3_node, pull_resistor_5_node, pull_resistor_7_node, pull_resistor_13_node, REG_CARRY_q,
       RESET_out, STEP_out, subtractor_1_bout;
  wire [2:0] counter_1_q, prog_data, prog_data_2, pull_resistor_6_node, pull_resistor_8_node,
       pull_resistor_10_node, pull_resistor_11_node, pull_resistor_12_node;
  wire [7:0] adder_1_out, and_6_out, controlled_buffer_15_out, controlled_buffer_16_out,
       controlled_buffer_17_out, controlled_buffer_18_out, controlled_buffer_19_out, multiplexer_1_out,
       multiplexer_3_out, not_2_out, or_5_out, pull_resistor_14_node, REG_A_q, REG_B_q, REG_C_q, REG_D_q,
       REG_E_q, REG_F_q, REG_H_q, REG_L_q, register_1_q, subtractor_1_out, xor_1_out;
  wire [7:6] prog_data_3;
  wire [8:0] decoder_1_out4, decoder_1_out6, decoder_1_out7, demultiplexer_1_out0, demultiplexer_1_out1,
       demultiplexer_1_out2, demultiplexer_1_out3, demultiplexer_1_out4, demultiplexer_1_out5,
       demultiplexer_1_out6, demultiplexer_1_out7, pull_resistor_9_node;
  wire [15:0] pull_resistor_4_node;
  wire [15:8] multiplexer_2_out;

  Clock clock_1 (.out(clock_1_out));
  Pull_Resistor pull_resistor_1 (.node(pull_resistor_1_node));
  buf buffer_1 (pull_resistor_1_node, clock_1_out);
  buf buffer_2 (pull_resistor_1_node, STEP_out);
  Button RESET (.out(RESET_out));
  Counter #(.max('h7), .width(3)) counter_1 (
    .clr(RESET_out), .load(pull_resistor_5_node), .clk(pull_resistor_1_node), .D(pull_resistor_6_node),
    .Q(counter_1_q));  // open: up, count, carry
  Comparator #(.width(3)) comparator_1 (.a(3'b000), .b(counter_1_q), .eq(comparator_1_eq));  // open: gt, lt
  Pull_Resistor pull_resistor_2 (.node(pull_resistor_2_node));
  buf buffer_3 (pull_resistor_2_node, comparator_1_eq);
  Counter #(.max('hffff), .width(16)) pc (
    .clr(RESET_out), .load(pull_resistor_3_node), .up(not_1_out), .clk(pull_resistor_2_node),
    .D(pull_resistor_4_node), .carry(pc_carry), .Q({decoder_1_out4[8:1], decoder_1_out6[8:1]}));  // open: count
  buf buffer_4 (pull_resistor_2_node, pull_resistor_7_node);
  buf buffer_5 (pull_resistor_2_node, pull_resistor_3_node);
  LED overflow (.in(pc_carry));
  ROM #(.addrWidth(16)) prog (
    .addr({decoder_1_out4[8:1], decoder_1_out6[8:1]}), .data({prog_data_3, prog_data_2, prog_data}));
  LED led_1 (.in(demultiplexer_1_out0[0]));
  LED led_2 (.in(demultiplexer_1_out1[0]));
  Button STEP (.out(STEP_out));
  LED led_3 (.in(demultiplexer_1_out2[0]));
  LED led_4 (.in(demultiplexer_1_out3[0]));
  LED led_5 (.in(demultiplexer_1_out4[0]));
  LED led_6 (.in(demultiplexer_1_out5[0]));
  LED led_7 (.in(demultiplexer_1_out6[0]));
  LED led_8 (.in(demultiplexer_1_out7[0]));
  Register REG_A (
    .D(demultiplexer_1_out0[8:1]), .clk(demultiplexer_1_out0[0]), .Q(REG_A_q), .clr(RESET_out));  // open: en
  Register REG_B (
    .D(demultiplexer_1_out1[8:1]), .clk(demultiplexer_1_out1[0]), .Q(REG_B_q), .clr(RESET_out));  // open: en
  Register REG_C (
    .D(demultiplexer_1_out2[8:1]), .clk(demultiplexer_1_out2[0]), .Q(REG_C_q), .clr(RESET_out));  // open: en
  Register REG_D (
    .D(demultiplexer_1_out3[8:1]), .clk(demultiplexer_1_out3[0]), .Q(REG_D_q), .clr(RESET_out));  // open: en
  Register REG_E (
    .D(demultiplexer_1_out4[8:1]), .clk(demultiplexer_1_out4[0]), .Q(REG_E_q), .clr(RESET_out));  // open: en
  Register REG_F (
    .D(demultiplexer_1_out5[8:1]), .clk(demultiplexer_1_out5[0]), .Q(REG_F_q), .clr(RESET_out));  // open: en
  Register REG_H (
    .D(demultiplexer_1_out6[8:1]), .clk(demultiplexer_1_out6[0]), .Q(REG_H_q), .clr(RESET_out));  // open: en
  Register REG_L (
    .D(demultiplexer_1_out7[8:1]), .clk(demultiplexer_1_out7[0]), .Q(REG_L_q), .clr(RESET_out));  // open: en
  Register register_1 (
    .D({prog_data_3, prog_data_2, prog_data}), .clk(decoder_1_out1), .Q(register_1_q), .clr(RESET_out));  // open: en
  Decoder #(.enable("false"), .select(3)) decoder_1 (
    .out0(decoder_1_out0), .out1(decoder_1_out1), .out2(decoder_1_out2), .out3(decoder_1_out3),
    .out4(decoder_1_out4[0]), .out5(decoder_1_out5), .out6(decoder_1_out6[0]), .out7(decoder_1_out7[0]),
    .sel(counter_1_q));
  Multiplexer #(.select(3), .width(8)) multiplexer_1 (
    .in0(REG_A_q), .in1(REG_B_q), .in2(REG_C_q), .in3(REG_D_q), .in4(REG_E_q), .in5(REG_F_q), .in6(REG_H_q),
    .in7(REG_L_q), .out(multiplexer_1_out), .sel(pull_resistor_12_node));
  Multiplexer #(.select(3), .width(8)) multiplexer_2 (
    .in0(REG_A_q), .in1(REG_B_q), .in2(REG_C_q), .in3(REG_D_q), .in4(REG_E_q), .in5(REG_F_q), .in6(REG_H_q),
    .in7(REG_L_q), .out(multiplexer_2_out), .sel(pull_resistor_11_node));
  Multiplexer #(.select(3), .width(8)) multiplexer_3 (
    .in0(REG_A_q), .in1(REG_B_q), .in2(REG_C_q), .in3(REG_D_q), .in4(REG_E_q), .in5(REG_F_q), .in6(REG_H_q),
    .in7(REG_L_q), .out(multiplexer_3_out), .sel(pull_resistor_10_node));
  Demultiplexer #(.select(3), .width(9)) demultiplexer_1 (
    .out0(demultiplexer_1_out0), .out1(demultiplexer_1_out1), .out2(demultiplexer_1_out2),
    .out3(demultiplexer_1_out3), .out4(demultiplexer_1_out4), .out5(demultiplexer_1_out5),
    .out6(demultiplexer_1_out6), .out7(demultiplexer_1_out7), .in(pull_resistor_9_node),
    .sel(pull_resistor_8_node));
  Pull_Resistor pull_resistor_3 (.node(pull_resistor_3_node));
  Pull_Resistor pull_resistor_4 (.node(pull_resistor_4_node));
  not not_1 (not_1_out, and_5_out);
  Pull_Resistor pull_resistor_5 (.node(pull_resistor_5_node));
  Pull_Resistor pull_resistor_6 (.node(pull_resistor_6_node));
  Pull_Resistor pull_resistor_7 (.node(pull_resistor_7_node));
  Pull_Resistor pull_resistor_8 (.node(pull_resistor_8_node));
  Pull_Resistor pull_resistor_9 (.node(pull_resistor_9_node));
  buf buffer_6 (pull_resistor_7_node, and_5_out);
  Pull_Resistor pull_resistor_10 (.node(pull_resistor_10_node));
  Pull_Resistor pull_resistor_11 (.node(pull_resistor_11_node));
  Pull_Resistor pull_resistor_12 (.node(pull_resistor_12_node));
  and and_1 (and_1_out, decoder_1_out2, comparator_2_eq);
  buf buffer_7 (pull_resistor_7_node, and_1_out);
  assign pull_resistor_12_node = comparator_2_eq ? prog_data : 3'bz;  // Controlled_Buffer controlled_buffer_1
  assign pull_resistor_11_node = comparator_2_eq ? prog_data_2 : 3'bz;  // Controlled_Buffer controlled_buffer_2
  assign pull_resistor_8_node = comparator_2_eq ? register_1_q[2:0] : 3'bz;  // Controlled_Buffer controlled_buffer_3
  assign pull_resistor_12_node = comparator_3_eq ? register_1_q[2:0] : 3'bz;  // Controlled_Buffer controlled_buffer_4
  assign pull_resistor_11_node = comparator_3_eq ? 3'b110 : 3'bz;  // Controlled_Buffer controlled_buffer_5
  assign pull_resistor_10_node = comparator_3_eq ? 3'b111 : 3'bz;  // Controlled_Buffer controlled_buffer_6
  assign pull_resistor_4_node = and_4_out ? {multiplexer_2_out, multiplexer_3_out} : 16'bz;  // Controlled_Buffer controlled_buffer_7
  buf buffer_8 (pull_resistor_3_node, and_4_out);
  or or_1 (or_1_out, decoder_1_out3, decoder_1_out4[0]);
  and and_2 (and_2_out, or_1_out, comparator_4_eq);
  assign pull_resistor_8_node = and_2_out ? 3'b110 : 3'bz;  // Controlled_Buffer controlled_buffer_8
  or or_2 (or_2_out, decoder_1_out6[0], decoder_1_out5);
  and and_3 (and_3_out, or_2_out, comparator_4_eq);
  assign pull_resistor_8_node = and_3_out ? 3'b111 : 3'bz;  // Controlled_Buffer controlled_buffer_9
  assign pull_resistor_9_node = and_2_out ? decoder_1_out4 : 9'bz;  // Controlled_Buffer controlled_buffer_10
  assign pull_resistor_9_node = and_3_out ? decoder_1_out6 : 9'bz;  // Controlled_Buffer controlled_buffer_11
  Comparator #(.mode("unsigned"), .width(1)) comparator_2 (
    .a(1'b1), .b(register_1_q[7]), .eq(comparator_2_eq));  // open: gt, lt
  LED instructions_1XXXXRRR (.in(comparator_2_eq));
  assign pull_resistor_9_node = comparator_2_eq ? decoder_1_out7 : 9'bz;  // Controlled_Buffer controlled_buffer_12
  Comparator #(.mode("unsigned"), .width(3)) comparator_3 (
    .a(3'b001), .b(register_1_q[7:5]), .eq(comparator_3_eq));  // open: gt, lt
  LED JUMPS_001XXRRR (.in(comparator_3_eq));
  Decoder #(.enable("false"), .select(2)) decoder_2 (
    .out0(decoder_2_out0), .out1(decoder_2_out1), .out2(decoder_2_out2), .sel(register_1_q[4:3]));  // open: out3
  and and_4 (and_4_out, decoder_1_out3, and_9_out);
  and and_5 (and_5_out, and_9_out, decoder_1_out5);
  Comparator #(.mode("unsigned"), .width(5)) comparator_4 (
    .a(5'b00010), .b(register_1_q[7:3]), .eq(comparator_4_eq));  // open: gt, lt
  LED PC_INS (.in(comparator_4_eq));
  Pull_Resistor pull_resistor_13 (.node(pull_resistor_13_node));
  assign pull_resistor_13_node = comparator_5_eq ? adder_1_cout : 1'bz;  // Controlled_Buffer controlled_buffer_13
  assign pull_resistor_13_node = comparator_9_eq ? subtractor_1_bout : 1'bz;  // Controlled_Buffer controlled_buffer_14
  Comparator #(.width(4)) comparator_5 (.a(register_1_q[6:3]), .b(4'b0000), .eq(comparator_5_eq));  // open: gt, lt
  Adder adder_1 (.a(multiplexer_2_out), .b(multiplexer_1_out), .out(adder_1_out), .cout(adder_1_cout));  // open: cin
  assign decoder_1_out7[8:1] = comparator_5_eq ? adder_1_out : 8'bz;  // Controlled_Buffer ADD
  assign decoder_1_out7[8:1] = comparator_6_eq ? and_6_out : 8'bz;  // Controlled_Buffer AND_INS
  assign and_6_out = multiplexer_1_out & multiplexer_2_out;  // AND_Gate and_6, 8 bits wide
  Comparator #(.width(4)) comparator_6 (.a(4'b0111), .b(register_1_q[6:3]), .eq(comparator_6_eq));  // open: gt, lt
  Comparator comparator_7 (.a(multiplexer_1_out), .b({8{1'b0}}), .eq(comparator_7_eq));  // open: gt, lt
  and and_7 (and_7_out, comparator_7_eq, decoder_2_out2);
  Comparator comparator_8 (.a(multiplexer_1_out), .b({8{1'b1}}), .eq(comparator_8_eq));  // open: gt, lt
  and and_8 (and_8_out, comparator_8_eq, decoder_2_out1);
  and and_9 (and_9_out, comparator_3_eq, or_3_out);
  or or_3 (or_3_out, and_7_out, and_8_out, decoder_2_out0);
  Register #(.width(1)) REG_CARRY (
    .D(pull_resistor_13_node), .clk(and_10_out), .Q(REG_CARRY_q), .clr(RESET_out));  // open: en
  and and_10 (and_10_out, decoder_1_out4[0], or_4_out);
  or or_4 (or_4_out, comparator_5_eq, comparator_9_eq);
  Comparator #(.width(4)) comparator_9 (.a(register_1_q[6:3]), .b(4'b0001), .eq(comparator_9_eq));  // open: gt, lt
  Subtractor subtractor_1 (
    .a(multiplexer_2_out), .b(multiplexer_1_out), .out(subtractor_1_out), .bout(subtractor_1_bout));  // open: bin
  assign or_5_out = multiplexer_1_out | multiplexer_2_out;  // OR_Gate or_5, 8 bits wide
  Comparator #(.width(4)) comparator_10 (.a(4'b1000), .b(register_1_q[6:3]), .eq(comparator_10_eq));  // open: gt, lt
  assign decoder_1_out7[8:1] = comparator_9_eq ? subtractor_1_out : 8'bz;  // Controlled_Buffer SUB
  assign decoder_1_out7[8:1] = comparator_10_eq ? or_5_out : 8'bz;  // Controlled_Buffer OR_INS
  Comparator #(.width(4)) comparator_11 (.a(register_1_q[6:3]), .b(4'b0010), .eq(comparator_11_eq));  // open: gt, lt
  or or_6 (or_6_out, comparator_12_eq, comparator_12_lt);
  Comparator comparator_12 (
    .a(multiplexer_2_out), .b(multiplexer_1_out), .eq(comparator_12_eq), .lt(comparator_12_lt));  // open: gt
  assign controlled_buffer_15_out = or_6_out ? {8{1'b1}} : 8'bz;  // Controlled_Buffer controlled_buffer_15
  assign decoder_1_out7[8:1] = comparator_11_eq ? controlled_buffer_15_out : 8'bz;  // Controlled_Buffer LTEQ
  assign decoder_1_out7[8:1] = comparator_13_eq ? xor_1_out : 8'bz;  // Controlled_Buffer XOR_INS
  assign xor_1_out = multiplexer_1_out ^ multiplexer_2_out;  // XOR_Gate xor_1, 8 bits wide
  Comparator #(.width(4)) comparator_13 (.a(4'b1001), .b(register_1_q[6:3]), .eq(comparator_13_eq));  // open: gt, lt
  RAM #(.addrWidth(16), .clearpin("true"), .enables("line"), .\type ("nonvolatile")) ram_1 (.clr(RESET_out));  // open: addr, we, clk, din, dout
  assign decoder_1_out7[8:1] = comparator_14_eq ? not_2_out : 8'bz;  // Controlled_Buffer NOT_INS
  assign not_2_out = ~multiplexer_1_out;  // NOT_Gate not_2, 8 bits wide
  Comparator #(.width(4)) comparator_14 (.a(4'b1010), .b(register_1_q[6:3]), .eq(comparator_14_eq));  // open: gt, lt
  Comparator #(.width(4)) comparator_15 (.a(register_1_q[6:3]), .b(4'b0011), .eq(comparator_15_eq));  // open: gt, lt
  or or_7 (or_7_out, comparator_16_gt, comparator_16_eq);
  Comparator comparator_16 (
    .a(multiplexer_2_out), .b(multiplexer_1_out), .gt(comparator_16_gt), .eq(comparator_16_eq));  // open: lt
  assign controlled_buffer_16_out = or_7_out ? {8{1'b1}} : 8'bz;  // Controlled_Buffer controlled_buffer_16
  assign decoder_1_out7[8:1] = comparator_15_eq ? controlled_buffer_16_out : 8'bz;  // Controlled_Buffer GTEQ
  Comparator #(.width(4)) comparator_17 (.a(4'b1011), .b(register_1_q[6:3]), .eq(comparator_17_eq));  // open: gt, lt
  Comparator #(.width(4)) comparator_18 (.a(register_1_q[6:3]), .b(4'b0100), .eq(comparator_18_eq));  // open: gt, lt
  Comparator comparator_19 (.a(multiplexer_2_out), .b(multiplexer_1_out), .lt(comparator_19_lt));  // open: gt, eq
  assign decoder_1_out7[8:1] = comparator_17_eq ? {prog_data_3, prog_data_2, prog_data} : 8'bz;  // Controlled_Buffer LDX
  assign controlled_buffer_17_out = comparator_19_lt ? {8{1'b1}} : 8'bz;  // Controlled_Buffer controlled_buffer_17
  assign decoder_1_out7[8:1] = comparator_18_eq ? controlled_buffer_17_out : 8'bz;  // Controlled_Buffer LT
  assign decoder_1_out7[8:1] = comparator_20_eq ? in_1 : 8'bz;  // Controlled_Buffer RI
  Comparator #(.width(4)) comparator_20 (.a(4'b1100), .b(register_1_q[6:3]), .eq(comparator_20_eq));  // open: gt, lt
  Comparator #(.width(4)) comparator_21 (.a(register_1_q[6:3]), .b(4'b0101), .eq(comparator_21_eq));  // open: gt, lt
  assign controlled_buffer_18_out = comparator_22_gt ? {8{1'b1}} : 8'bz;  // Controlled_Buffer controlled_buffer_18
  Comparator comparator_22 (.a(multiplexer_2_out), .b(multiplexer_1_out), .gt(comparator_22_gt));  // open: eq, lt
  assign decoder_1_out7[8:1] = comparator_21_eq ? controlled_buffer_18_out : 8'bz;  // Controlled_Buffer GT
  Comparator #(.width(4)) comparator_23 (.a(4'b1101), .b(register_1_q[6:3]), .eq(comparator_23_eq));  // open: gt, lt
  Comparator #(.width(4)) comparator_24 (.a(register_1_q[6:3]), .b(4'b0110), .eq(comparator_24_eq));  // open: gt, lt
  Comparator comparator_25 (.a(multiplexer_2_out), .b(multiplexer_1_out), .eq(comparator_25_eq));  // open: gt, lt
  assign controlled_buffer_19_out = comparator_25_eq ? {8{1'b1}} : 8'bz;  // Controlled_Buffer controlled_buffer_19
  assign decoder_1_out7[8:1] = comparator_24_eq ? controlled_buffer_19_out : 8'bz;  // Controlled_Buffer EQ
  assign decoder_1_out7[8:1] = comparator_23_eq ? pull_resistor_14_node : 8'bz;  // Controlled_Buffer CARRY
  Pull_Resistor pull_resistor_14 (.node(pull_resistor_14_node));
  assign pull_resistor_14_node = REG_CARRY_q ? {8{1'b1}} : 8'bz;  // Controlled_Buffer controlled_buffer_20

  // Notes on the sheet:
  //   buffer_1 drives only 1 and floats otherwise
  //   buffer_2 drives only 1 and floats otherwise
  //   buffer_3 drives only 1 and floats otherwise
  //   buffer_4 drives only 1 and floats otherwise
  //   buffer_5 drives only 1 and floats otherwise
  //   contents of prog (hex, n*v repeats v):
  //   d8 0 d9 6 82 1 10 e8 11*0 20 0 30
  //   buffer_6 drives only 1 and floats otherwise
  //   buffer_7 drives only 1 and floats otherwise
  //   buffer_8 drives only 1 and floats otherwise
endmodule
