// Logisim project project.circ as structural Verilog: 1 circuit, main circuit main
module main (
);

  wire and_2_out, and_3_out, and_4_out, and_5_out, and_6_out, and_7_out, and_8_out, and_9_out, and_10_out,
       and_11_out, and_12_out, and_13_out, and_14_out, and_15_out, and_16_out, and_17_out, and_18_out,
       and_19_out, and_20_out, and_21_out, clock_1_out, comparator_1_eq, comparator_2_eq, comparator_5_eq,
       comparator_6_eq, comparator_7_eq, comparator_8_eq, comparator_9_eq, comparator_9_lt, comparator_10_eq,
       comparator_11_eq, comparator_11_gt, comparator_12_eq, comparator_14_eq, comparator_16_eq,
       comparator_18_eq, comparator_19_eq, comparator_20_eq, comparator_21_eq, comparator_22_eq,
       comparator_23_eq, comparator_24_eq, comparator_25_eq, comparator_26_eq, comparator_27_eq,
       comparator_28_eq, comparator_29_eq, not_1_out, pc_carry, pull_resistor_1_node, pull_resistor_2_node,
       pull_resistor_3_node, pull_resistor_4_node, pull_resistor_6_node, pull_resistor_7_node,
       pull_resistor_8_node, pull_resistor_9_node, pull_resistor_10_node, pull_resistor_11_node,
       pull_resistor_12_node, RESET_out, STEP_out;
  wire [0:0] adder_1_cout, subtractor_1_bout;
  wire [1:0] counter_1_q, REG_FLAGS_q_2, undriven;
  wire [3:0] REG_A_q, REG_A_q_2;
  wire [4:0] REG_FLAGS_q_3;
  wire [7:0] adder_1_out, and_1_out, controlled_buffer_1_out, controlled_buffer_12_out,
       controlled_buffer_13_out, controlled_buffer_15_out, not_2_out, or_1_out, pc_q, pc_q_2, prog_data,
       REG_NOP_out, subtractor_1_out, xor_1_out;
  wire [7:7] comparator_13_lt, comparator_15_gt, comparator_17_eq, or_2_out, or_3_out, REG_FLAGS_q;
  wire [15:0] controlled_buffer_18_out, REG_B_q;

  Clock clock_1 (.out(clock_1_out));
  Pull_Resistor pull_resistor_1 (.node(pull_resistor_1_node));
  buf buffer_1 (pull_resistor_1_node, clock_1_out);
  buf buffer_2 (pull_resistor_1_node, STEP_out);
  Counter #(.max('h3), .width(2)) counter_1 (
    .clr(RESET_out), .load(pull_resistor_12_node), .clk(pull_resistor_1_node), .D(undriven), .Q(counter_1_q));  // open: up, count, carry
  Button RESET (.out(RESET_out));
  Pull_Resistor pull_resistor_2 (.node(pull_resistor_2_node));
  buf buffer_3 (pull_resistor_2_node, comparator_1_eq);
  Comparator #(.width(2)) comparator_1 (.a(2'b00), .b(counter_1_q), .eq(comparator_1_eq));  // open: gt, lt
  Counter #(.max('hffff), .width(16)) pc (
    .clr(RESET_out), .load(pull_resistor_8_node), .clk(pull_resistor_2_node), .D(controlled_buffer_18_out),
    .carry(pc_carry), .Q({pc_q_2, pc_q}));  // open: up, count
  buf buffer_4 (pull_resistor_2_node, pull_resistor_8_node);
  LED overflow (.in(pc_carry));
  Button STEP (.out(STEP_out));
  ROM #(.addrWidth(16)) prog (.addr({pc_q_2, pc_q}), .data(prog_data));
  Hex_Digit_Display hex_digit_display_1 (.value(REG_A_q_2));  // open: dp
  Hex_Digit_Display hex_digit_display_2 (.value(REG_B_q[7:4]));  // open: dp
  Hex_Digit_Display hex_digit_display_3 (.value(REG_B_q[15:12]));  // open: dp
  Hex_Digit_Display hex_digit_display_4 (.value(REG_A_q));  // open: dp
  Hex_Digit_Display hex_digit_display_5 (.value(REG_B_q[3:0]));  // open: dp
  Hex_Digit_Display hex_digit_display_6 (.value(REG_B_q[11:8]));  // open: dp
  Register REG_A (
    .D(controlled_buffer_1_out), .clk(pull_resistor_3_node), .Q({REG_A_q_2, REG_A_q}), .clr(RESET_out));  // open: en
  LED led_1 (.in(pull_resistor_3_node));
  Register REG_B (
    .D(controlled_buffer_12_out), .clk(pull_resistor_4_node), .Q(REG_B_q[7:0]), .clr(RESET_out));  // open: en
  LED led_2 (.in(pull_resistor_4_node));
  Register REG_C (
    .D(controlled_buffer_13_out), .clk(pull_resistor_4_node), .Q(REG_B_q[15:8]), .clr(RESET_out));  // open: en
  LED led_3 (.in(pull_resistor_4_node));
  Register REG_FLAGS (
    .D(controlled_buffer_15_out), .clk(pull_resistor_7_node),
    .Q({REG_FLAGS_q_3, REG_FLAGS_q_2, REG_FLAGS_q[7]}), .clr(RESET_out));  // open: en
  LED led_4 (.in(pull_resistor_7_node));
  Pull_Resistor pull_resistor_3 (.node(pull_resistor_3_node));
  Pull_Resistor pull_resistor_4 (.node(pull_resistor_4_node));
  Pull_Resistor pull_resistor_5 (.node(pull_resistor_4_node));
  Comparator #(.width(2)) comparator_2 (.a(2'b00), .b(REG_FLAGS_q_2), .eq(comparator_2_eq));  // open: gt, lt
  Pull_Resistor pull_resistor_6 (.node(pull_resistor_6_node));
  Pull_Resistor pull_resistor_7 (.node(pull_resistor_7_node));
  Pull_Resistor pull_resistor_8 (.node(pull_resistor_8_node));
  Pull_Resistor pull_resistor_9 (.node(pull_resistor_9_node));
  Pull_Resistor pull_resistor_10 (.node(pull_resistor_10_node));
  Pull_Resistor pull_resistor_11 (.node(pull_resistor_11_node));
  Pull_Resistor pull_resistor_12 (.node(pull_resistor_12_node));
  not not_1 (not_1_out, comparator_2_eq);
  assign REG_NOP_out = comparator_2_eq ? prog_data : 8'bz;  // Controlled_Buffer REG_NOP
  Pull_Resistor pull_resistor_13 (.node(REG_NOP_out));
  assign controlled_buffer_1_out = comparator_6_eq ? adder_1_out : 8'bz;  // Controlled_Buffer controlled_buffer_1
  buf buffer_5 (pull_resistor_3_node, and_4_out);
  buf buffer_6 (pull_resistor_7_node, and_4_out);
  assign controlled_buffer_1_out = comparator_7_eq ? subtractor_1_out : 8'bz;  // Controlled_Buffer controlled_buffer_2
  buf buffer_7 (pull_resistor_3_node, and_5_out);
  buf buffer_8 (pull_resistor_7_node, and_5_out);
  assign controlled_buffer_1_out = comparator_8_eq ? {8{or_2_out[7]}} : 8'bz;  // Controlled_Buffer controlled_buffer_3
  assign controlled_buffer_1_out = comparator_10_eq ? {8{or_3_out[7]}} : 8'bz;  // Controlled_Buffer controlled_buffer_4
  assign controlled_buffer_1_out = comparator_12_eq ? {8{comparator_13_lt[7]}} : 8'bz;  // Controlled_Buffer controlled_buffer_5
  assign controlled_buffer_1_out = comparator_14_eq ? {8{comparator_15_gt[7]}} : 8'bz;  // Controlled_Buffer controlled_buffer_6
  assign controlled_buffer_1_out = comparator_16_eq ? {8{comparator_17_eq[7]}} : 8'bz;  // Controlled_Buffer controlled_buffer_7
  assign controlled_buffer_1_out = comparator_18_eq ? and_1_out : 8'bz;  // Controlled_Buffer controlled_buffer_8
  assign controlled_buffer_1_out = comparator_19_eq ? or_1_out : 8'bz;  // Controlled_Buffer controlled_buffer_9
  assign controlled_buffer_1_out = comparator_20_eq ? xor_1_out : 8'bz;  // Controlled_Buffer controlled_buffer_10
  assign controlled_buffer_1_out = comparator_21_eq ? not_2_out : 8'bz;  // Controlled_Buffer controlled_buffer_11
  assign controlled_buffer_12_out = comparator_22_eq ? pc_q : 8'bz;  // Controlled_Buffer controlled_buffer_12
  assign controlled_buffer_13_out = comparator_22_eq ? pc_q_2 : 8'bz;  // Controlled_Buffer controlled_buffer_13
  assign controlled_buffer_1_out = comparator_23_eq ? {8{REG_FLAGS_q[7]}} : 8'bz;  // Controlled_Buffer controlled_buffer_14
  buf buffer_9 (pull_resistor_7_node, and_20_out);
  assign controlled_buffer_15_out = and_20_out ? {REG_FLAGS_q_3, 2'b01, REG_FLAGS_q[7]} : 8'bz;  // Controlled_Buffer controlled_buffer_15
  Comparator #(.width(2)) comparator_3 (.a(2'b00), .b(counter_1_q), .eq(pull_resistor_6_node));  // open: gt, lt
  Comparator #(.width(2)) comparator_4 (.a(2'b01), .b(counter_1_q), .eq(pull_resistor_9_node));  // open: gt, lt
  Comparator comparator_5 (.a(REG_NOP_out), .b({8{1'b0}}), .eq(comparator_5_eq));  // open: gt, lt
  LED NOP (.in(comparator_5_eq));
  Comparator comparator_6 (.a(REG_NOP_out), .b(8'h1), .eq(comparator_6_eq));  // open: gt, lt
  LED ADD (.in(comparator_6_eq));
  assign controlled_buffer_15_out = comparator_6_eq ? {REG_FLAGS_q_3, REG_FLAGS_q_2, adder_1_cout[0]} : 8'bz;  // Controlled_Buffer controlled_buffer_16
  Comparator comparator_7 (.a(REG_NOP_out), .b(8'h2), .eq(comparator_7_eq));  // open: gt, lt
  LED SUB (.in(comparator_7_eq));
  assign controlled_buffer_15_out = comparator_7_eq ? {REG_FLAGS_q_3, REG_FLAGS_q_2, subtractor_1_bout[0]} : 8'bz;  // Controlled_Buffer controlled_buffer_17
  Comparator comparator_8 (.a(REG_NOP_out), .b(8'h10), .eq(comparator_8_eq));  // open: gt, lt
  LED LTEQ (.in(comparator_8_eq));
  Comparator #(.mode("unsigned")) comparator_9 (
    .a({REG_A_q_2, REG_A_q}), .b(REG_B_q[7:0]), .eq(comparator_9_eq), .lt(comparator_9_lt));  // open: gt
  Comparator comparator_10 (.a(REG_NOP_out), .b(8'h11), .eq(comparator_10_eq));  // open: gt, lt
  LED GTEQ (.in(comparator_10_eq));
  Comparator #(.mode("unsigned")) comparator_11 (
    .a({REG_A_q_2, REG_A_q}), .b(REG_B_q[7:0]), .gt(comparator_11_gt), .eq(comparator_11_eq));  // open: lt
  Comparator comparator_12 (.a(REG_NOP_out), .b(8'h12), .eq(comparator_12_eq));  // open: gt, lt
  LED LT (.in(comparator_12_eq));
  Comparator #(.mode("unsigned")) comparator_13 (
    .a({REG_A_q_2, REG_A_q}), .b(REG_B_q[7:0]), .lt(comparator_13_lt[7]));  // open: gt, eq
  Comparator comparator_14 (.a(REG_NOP_out), .b(8'h13), .eq(comparator_14_eq));  // open: gt, lt
  LED GT (.in(comparator_14_eq));
  Comparator #(.mode("unsigned")) comparator_15 (
    .a({REG_A_q_2, REG_A_q}), .b(REG_B_q[7:0]), .gt(comparator_15_gt[7]));  // open: eq, lt
  Comparator comparator_16 (.a(REG_NOP_out), .b(8'h14), .eq(comparator_16_eq));  // open: gt, lt
  LED EQ (.in(comparator_16_eq));
  Comparator #(.mode("unsigned")) comparator_17 (
    .a({REG_A_q_2, REG_A_q}), .b(REG_B_q[7:0]), .eq(comparator_17_eq[7]));  // open: gt, lt
  Comparator comparator_18 (.a(REG_NOP_out), .b(8'h20), .eq(comparator_18_eq));  // open: gt, lt
  LED AND_BITWISE (.in(comparator_18_eq));
  assign and_1_out = {REG_A_q_2, REG_A_q} & REG_B_q[7:0];  // AND_Gate and_1, 8 bits wide
  Comparator comparator_19 (.a(REG_NOP_out), .b(8'h21), .eq(comparator_19_eq));  // open: gt, lt
  LED OR_BITWISE (.in(comparator_19_eq));
  assign or_1_out = {REG_A_q_2, REG_A_q} | REG_B_q[7:0];  // OR_Gate or_1, 8 bits wide
  Comparator comparator_20 (.a(REG_NOP_out), .b(8'h22), .eq(comparator_20_eq));  // open: gt, lt
  LED XOR_BITWISE (.in(comparator_20_eq));
  assign xor_1_out = {REG_A_q_2, REG_A_q} ^ REG_B_q[7:0];  // XOR_Gate xor_1, 8 bits wide
  Comparator comparator_21 (.a(REG_NOP_out), .b(8'h23), .eq(comparator_21_eq));  // open: gt, lt
  LED NOT_BITWISE (.in(comparator_21_eq));
  assign not_2_out = ~{REG_A_q_2, REG_A_q};  // NOT_Gate not_2, 8 bits wide
  Comparator comparator_22 (.a(REG_NOP_out), .b(8'h30), .eq(comparator_22_eq));  // open: gt, lt
  LED GET_PC (.in(comparator_22_eq));
  Comparator comparator_23 (.a(REG_NOP_out), .b(8'h31), .eq(comparator_23_eq));  // open: gt, lt
  LED GET_CARRY (.in(comparator_23_eq));
  Comparator comparator_24 (.a(REG_NOP_out), .b(8'h40), .eq(comparator_24_eq));  // open: gt, lt
  LED JUMP (.in(comparator_24_eq));
  buf buffer_10 (pull_resistor_8_node, and_17_out);
  assign controlled_buffer_18_out = and_17_out ? REG_B_q : 16'bz;  // Controlled_Buffer controlled_buffer_18
  Comparator comparator_25 (.a(REG_NOP_out), .b(8'h41), .eq(comparator_25_eq));  // open: gt, lt
  LED JUMPI (.in(comparator_25_eq));
  buf buffer_11 (pull_resistor_8_node, and_2_out);
  and and_2 (and_2_out, and_18_out, comparator_26_eq);
  assign controlled_buffer_18_out = and_2_out ? REG_B_q : 16'bz;  // Controlled_Buffer controlled_buffer_19
  Comparator comparator_26 (.a({REG_A_q_2, REG_A_q}), .b({8{1'b1}}), .eq(comparator_26_eq));  // open: gt, lt
  Comparator comparator_27 (.a(REG_NOP_out), .b(8'h42), .eq(comparator_27_eq));  // open: gt, lt
  LED JUMPZ (.in(comparator_27_eq));
  buf buffer_12 (pull_resistor_8_node, and_3_out);
  and and_3 (and_3_out, and_19_out, comparator_28_eq);
  assign controlled_buffer_18_out = and_3_out ? REG_B_q : 16'bz;  // Controlled_Buffer controlled_buffer_20
  Comparator comparator_28 (.a({REG_A_q_2, REG_A_q}), .b({8{1'b0}}), .eq(comparator_28_eq));  // open: gt, lt
  Comparator comparator_29 (.a(REG_NOP_out), .b(8'h60), .eq(comparator_29_eq));  // open: gt, lt
  LED LDA (.in(comparator_29_eq));
  Comparator #(.width(2)) comparator_30 (.a(2'b10), .b(counter_1_q), .eq(pull_resistor_10_node));  // open: gt, lt
  and and_4 (and_4_out, pull_resistor_9_node, comparator_6_eq);
  Adder adder_1 (.a({REG_A_q_2, REG_A_q}), .b(REG_B_q[7:0]), .out(adder_1_out), .cout(adder_1_cout[0]));  // open: cin
  and and_5 (and_5_out, pull_resistor_9_node, comparator_7_eq);
  Subtractor subtractor_1 (
    .a({REG_A_q_2, REG_A_q}), .b(REG_B_q[7:0]), .out(subtractor_1_out), .bout(subtractor_1_bout[0]));  // open: bin
  or or_2 (or_2_out[7], comparator_9_eq, comparator_9_lt);
  and and_6 (and_6_out, pull_resistor_9_node, comparator_8_eq);
  buf buffer_13 (pull_resistor_3_node, and_6_out);
  or or_3 (or_3_out[7], comparator_11_gt, comparator_11_eq);
  and and_7 (and_7_out, pull_resistor_9_node, comparator_10_eq);
  buf buffer_14 (pull_resistor_3_node, and_7_out);
  and and_8 (and_8_out, pull_resistor_9_node, comparator_12_eq);
  buf buffer_15 (pull_resistor_3_node, and_8_out);
  and and_9 (and_9_out, pull_resistor_9_node, comparator_14_eq);
  buf buffer_16 (pull_resistor_3_node, and_9_out);
  and and_10 (and_10_out, pull_resistor_9_node, comparator_16_eq);
  buf buffer_17 (pull_resistor_3_node, and_10_out);
  and and_11 (and_11_out, pull_resistor_9_node, comparator_18_eq);
  buf buffer_18 (pull_resistor_3_node, and_11_out);
  and and_12 (and_12_out, pull_resistor_9_node, comparator_19_eq);
  buf buffer_19 (pull_resistor_3_node, and_12_out);
  and and_13 (and_13_out, pull_resistor_9_node, comparator_20_eq);
  buf buffer_20 (pull_resistor_3_node, and_13_out);
  and and_14 (and_14_out, pull_resistor_9_node, comparator_21_eq);
  buf buffer_21 (pull_resistor_3_node, and_14_out);
  and and_15 (and_15_out, pull_resistor_9_node, comparator_22_eq);
  buf buffer_22 (pull_resistor_4_node, and_15_out);
  and and_16 (and_16_out, pull_resistor_9_node, comparator_23_eq);
  buf buffer_23 (pull_resistor_3_node, and_16_out);
  and and_17 (and_17_out, pull_resistor_10_node, comparator_24_eq);
  and and_18 (and_18_out, pull_resistor_10_node, comparator_25_eq);
  and and_19 (and_19_out, pull_resistor_10_node, comparator_27_eq);
  and and_20 (and_20_out, pull_resistor_11_node, comparator_29_eq);
  Comparator #(.width(2)) comparator_31 (.a(2'b11), .b(counter_1_q), .eq(pull_resistor_11_node));  // open: gt, lt
  and and_21 (and_21_out, not_1_out, pull_resistor_9_node);
  Comparator #(.width(2)) comparator_32 (.a(2'b01), .b(REG_FLAGS_q_2));  // open: gt, eq, lt
  Comparator #(.width(2)) comparator_33 (.a(2'b10), .b(REG_FLAGS_q_2));  // open: gt, eq, lt
  Comparator #(.width(2)) comparator_34 (.a(2'b11), .b(REG_FLAGS_q_2));  // open: gt, eq, lt

  // Notes on the sheet:
  //   buffer_1 drives only 1 and floats otherwise
  //   buffer_2 drives only 1 and floats otherwise
  //   buffer_3 drives only 1 and floats otherwise
  //   buffer_4 drives only 1 and floats otherwise
  //   contents of prog (hex, n*v repeats v):
  //   60 1 1 61 0 62 d 41 61 0 62 0 40 12
  //   buffer_5 drives only 1 and floats otherwise
  //   buffer_6 drives only 1 and floats otherwise
  //   buffer_7 drives only 1 and floats otherwise
  //   buffer_8 drives only 1 and floats otherwise
  //   buffer_9 drives only 1 and floats otherwise
  //   buffer_10 drives only 1 and floats otherwise
  //   buffer_11 drives only 1 and floats otherwise
  //   buffer_12 drives only 1 and floats otherwise
  //   buffer_13 drives only 1 and floats otherwise
  //   buffer_14 drives only 1 and floats otherwise
  //   buffer_15 drives only 1 and floats otherwise
  //   buffer_16 drives only 1 and floats otherwise
  //   buffer_17 drives only 1 and floats otherwise
  //   buffer_18 drives only 1 and floats otherwise
  //   buffer_19 drives only 1 and floats otherwise
  //   buffer_20 drives only 1 and floats otherwise
  //   buffer_21 drives only 1 and floats otherwise
  //   buffer_22 drives only 1 and floats otherwise
  //   buffer_23 drives only 1 and floats otherwise
endmodule
